// Digital circuit MMU.dig as structural Verilog
module MMU (
  input  Ctrl_Alloc,
  input  Ctrl_Dealloc,
  input  Ctrl_AllocOut,
  input  [31:0] Bus,
  input  [31:0] MemDataIn,
  input  Clk,
  output [31:0] MemAddr,
  output [31:0] MemDataOut,
  output MemStr,
  output MemLd,
  output CPU_Enable
);

  wire comparator_1_eq, comparator_1_gt, or_1_out, or_2_out, Step_ovf;
  wire [8:1] or_3_out;
  wire [23:0] Microcode_d;
  wire [31:0] add_1_s, Available_q, Desired_q, First_q, Next_q, Previous_q, pulldown_1_out, Split_s, sub_1_s,
       Testing_q;

  Register #(.Bits(3)) State (.D(Microcode_d[23:21]), .C(Clk), .en(Microcode_d[20]), .Q(or_3_out[8:6]));
  Counter #(.Bits(3)) Step (.en(1'b1), .C(Clk), .clr(or_1_out), .out(or_3_out[5:3]), .ovf(Step_ovf));
  or or_1 (or_1_out, Microcode_d[20], Step_ovf);
  // Probe on or_3_out[8:6]
  // Probe on or_3_out[5:3]
  ROM #(.bigEndian("true"), .AddrBits(9), .Bits(24)) Microcode (
    .A({or_3_out, Ctrl_Alloc}), .sel(1'b1),
    .D({Microcode_d[23:19], CPU_Enable, MemStr, MemLd, Microcode_d[15:0]}));
  // Probe on {Microcode_d[23:19], CPU_Enable, MemStr, MemLd, Microcode_d[15:0]}
  PullDown #(.Bits(32)) pulldown_1 (.out(pulldown_1_out));
  Register #(.Bits(32)) Available (.D(pulldown_1_out), .C(Clk), .en(Microcode_d[0]), .Q(Available_q));
  assign pulldown_1_out = Microcode_d[1] ? Available_q : 32'bz;  // Driver driver_1
  Register #(.Bits(32)) Desired (.D(Bus), .C(Clk), .en(Microcode_d[2]), .Q(Desired_q));
  assign pulldown_1_out = Microcode_d[3] ? Desired_q : 32'bz;  // Driver driver_2
  Comparator #(.Bits(32)) comparator_1 (
    .a(Available_q), .b(Desired_q), .gt(comparator_1_gt), .eq(comparator_1_eq));  // open: lt
  Sub #(.Bits(32)) sub_1 (.a(Available_q), .b(Desired_q), .c_i(1'b0), .s(sub_1_s));  // open: c_o
  Add add_1 (.a(pulldown_1_out[0]), .b(Microcode_d[15]), .c_i(1'b0), .s(add_1_s[0]));  // open: c_o
  or or_2 (or_2_out, Microcode_d[14], Microcode_d[15]);
  assign pulldown_1_out = MemLd ? MemDataIn : 32'bz;  // Driver driver_3
  assign MemDataOut = MemStr ? pulldown_1_out : 32'bz;  // Driver driver_4
  or or_3 (or_3_out[2], comparator_1_gt, comparator_1_eq);
  assign pulldown_1_out = Microcode_d[4] ? sub_1_s : 32'bz;  // Driver driver_5
  Register #(.Bits(32)) register_1 (.D(add_1_s), .C(Clk), .en(or_2_out), .Q(MemAddr));
  Register #(.Bits(32)) First (.D(pulldown_1_out), .C(Clk), .en(Microcode_d[5]), .Q(First_q));
  assign pulldown_1_out = Microcode_d[6] ? First_q : 32'bz;  // Driver driver_6
  Register #(.Bits(32)) Previous (.D(pulldown_1_out), .C(Clk), .en(Microcode_d[7]), .Q(Previous_q));
  assign pulldown_1_out = Microcode_d[8] ? Previous_q : 32'bz;  // Driver driver_7
  Register #(.Bits(32)) Testing (.D(pulldown_1_out), .C(Clk), .en(Microcode_d[9]), .Q(Testing_q));
  assign pulldown_1_out = Microcode_d[10] ? Testing_q : 32'bz;  // Driver driver_8
  assign pulldown_1_out = Microcode_d[11] ? Split_s : 32'bz;  // Driver driver_9
  Register #(.Bits(32)) Next (.D(pulldown_1_out), .C(Clk), .en(Microcode_d[12]), .Q(Next_q));
  assign pulldown_1_out = Microcode_d[13] ? Next_q : 32'bz;  // Driver driver_10
  Comparator comparator_2 (.a(First_q[0]), .b(Previous_q[0]), .eq(or_3_out[1]));  // open: gt, lt
  Add #(.Bits(32)) Split (.a(Testing_q), .b(Desired_q), .c_i(1'b0), .s(Split_s));  // open: c_o
  // Pins of 1 and 32 bits meet at pulldown_1_out
  // Pins of 1 and 32 bits meet at First_q
  // Pins of 1 and 32 bits meet at Previous_q
  // Pins of 1 and 32 bits meet at add_1_s

  // Notes on the sheet:
  //   CPU_Enable: Pulled low to suspend bytecode execution during allocation and deallocation operations
  //   Microcode loads MMU-ucode.bin
  //   Sufficient
  //   Remaining
  //   PreviousIsFirst
endmodule
